# Fritzing sketch dc_motor_control (saved by Fritzing 0.9.3b)
breadboards: 1

parts:
  D1 = Rectifier Diode [part_number=1N4001 package="300 mil [THT]"]
  R1 = Resistor [tolerance=±5% resistance=270 package=THT]
  Part1 = Adafruit Pro Trinket 5V 16MHz [part_number="Adafruit #2000"]
  Q1 = NPN-Transistor [package="TO92 [THT]"]
  PSU1 = Adjustable Breadboard Power Supply
  M1 = DC Motor
  M2 = DC Motor

nets:
  N1: D1.cathode, PSU1.Vo+, M1.pin_1, M2.pin_1
  N2: D1.anode, Q1.C, M1.pin_2, M2.pin_2
  N3: R1.Pin_0, Q1.B
  N4: R1.Pin_1, Part1.D3
  N5: Part1.GND, Q1.E, PSU1.Vo-

custom parts:
  Adafruit Pro Trinket 5V 16MHz: Trinket's got a big sister in town - the Pro Trinket 5V! Pro Trinket combines everything you love about Trinket with the familiarity of the common core Arduino chip, the ATmega328. It's like an Arduino Pro Mini with more pins and USB tossed in, so delicious. Trinket's a year old now, and while its been great to see tons of tiny projects, sometimes you just need more pins, more FLASH, and more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
